// Logisim project aulaoAc1.circ as structural Verilog
module main (
  input  a,
  input  b,
  output x
);

  wire and_1_out, and_2_out, not_1_out, not_2_out;

  not not_1 (not_1_out, a);
  not not_2 (not_2_out, b);
  and and_1 (and_1_out, not_1_out, b);
  and and_2 (and_2_out, a, not_2_out);
  or or_1 (x, and_1_out, and_2_out);
endmodule

module meio_somador (
  input  a,
  input  b,
  output s0,
  output vai1
);

  xor xor_1 (s0, a, b);
  and and_1 (vai1, a, b);
endmodule

module somador_completo (
  input  vem1,
  input  a,
  input  b,
  output out_4,
  output out_5
);

  wire meio_somador_1_s0, meio_somador_1_vai1, meio_somador_2_vai1;

  meio_somador meio_somador_1 (.a(a), .b(b), .s0(meio_somador_1_s0), .vai1(meio_somador_1_vai1));
  meio_somador meio_somador_2 (.a(meio_somador_1_s0), .b(vem1), .s0(out_4), .vai1(meio_somador_2_vai1));
  or or_1 (out_5, meio_somador_2_vai1, meio_somador_1_vai1);
endmodule

module somador_de_4 (
  input  [3:0] a,
  input  [3:0] b,
  input  vem1,
  output [3:0] s,
  output [4:0] s_2,
  output vai1
);

  wire somador_completo_1_out_5, somador_completo_2_out_5, somador_completo_3_out_5;

  // Probe on a
  // Probe on b
  somador_completo somador_completo_1 (.vem1(vem1), .a(b[0]), .b(a[0]), .out_4(s[0]), .out_5(somador_completo_1_out_5));
  somador_completo somador_completo_2 (
    .vem1(somador_completo_1_out_5), .a(b[1]), .b(a[1]), .out_4(s[1]), .out_5(somador_completo_2_out_5));
  somador_completo somador_completo_3 (
    .vem1(somador_completo_2_out_5), .a(b[2]), .b(a[2]), .out_4(s[2]), .out_5(somador_completo_3_out_5));
  somador_completo somador_completo_4 (
    .vem1(somador_completo_3_out_5), .a(b[3]), .b(a[3]), .out_4(s[3]), .out_5(s_2[4]));
  // Probe on s
  // Probe on {s_2[4], s}

  assign s_2[3:0] = s;
  assign vai1 = s_2[4];
endmodule

module MUX (
  input  a,
  input  coisa,
  input  b,
  input  permissor,
  input  permissor_2,
  input  in_6,
  input  in_7,
  input  in_8,
  input  in_9,
  input  in_10,
  input  in_11,
  input  in_12,
  input  in_13,
  input  in_14,
  input  in_15,
  input  in_16,
  input  in_17,
  output a_b,
  output coisa_ou_0,
  output out_20,
  output out_21
);

  wire and_2_out, and_3_out, and_4_out, and_5_out, and_6_out, and_7_out, not_1_out, not_2_out, not_3_out,
       not_4_out, not_5_out;

  and and_1 (coisa_ou_0, coisa, permissor);
  not not_1 (not_1_out, permissor_2);
  and and_2 (and_2_out, in_6, not_2_out, not_3_out);
  not not_2 (not_2_out, in_16);
  not not_3 (not_3_out, in_17);
  not not_4 (not_4_out, in_16);
  and and_3 (and_3_out, in_9, not_4_out, in_17);
  and and_4 (and_4_out, in_12, in_16, not_5_out);
  not not_5 (not_5_out, in_17);
  and and_5 (and_5_out, in_14, in_16, in_17);
  and and_6 (and_6_out, a, not_1_out);
  or or_1 (a_b, and_6_out, and_7_out);
  and and_7 (and_7_out, b, permissor_2);
  or or_2 (out_21, and_2_out, and_3_out, and_4_out, and_5_out);
  Multiplexer #(.select(2), .enable("false")) multiplexer_1 (
    .in0(in_7), .in1(in_8), .in2(in_10), .in3(in_11), .out(out_20), .sel({in_13, in_15}));

  // Notes on the sheet:
  //   ------>
  //   pega o que passar
endmodule

module DMUX (
  input  coisa,
  input  coisa_2,
  input  onde,
  input  in_4,
  input  onde_2,
  output out_6,
  output out_7,
  output out_8,
  output out_9,
  output out_10,
  output out_11
);

  wire not_1_out, not_2_out, not_3_out, not_4_out, not_5_out;

  not not_1 (not_1_out, onde);
  and and_1 (out_6, coisa, not_1_out);
  and and_2 (out_9, coisa, onde);
  not not_2 (not_2_out, in_4);
  and and_3 (out_7, coisa_2, not_2_out, not_3_out);
  not not_3 (not_3_out, onde_2);
  not not_4 (not_4_out, in_4);
  and and_4 (out_8, coisa_2, not_4_out, onde_2);
  and and_5 (out_10, coisa_2, in_4, not_5_out);
  not not_5 (not_5_out, onde_2);
  and and_6 (out_11, coisa_2, in_4, onde_2);

  // Notes on the sheet:
  //   --------->
  //   onde ela sai
endmodule

module meio_subrator (
  input  a,
  input  b,
  output s,
  output deve1
);

  wire not_1_out;

  not not_1 (not_1_out, a);
  xor xor_1 (s, a, b);
  and and_1 (deve1, b, not_1_out);
endmodule
