// Logisim project Portas_Com_NAND_e_NOR.circ as structural Verilog: 5 circuits, main circuit NOT
module NOT (
  input  a,
  input  b,
  output na,
  output nb
);

  nand nand_1 (na, a, a);
  nor nor_1 (nb, b, b);
endmodule

module AND (
  input  a,
  input  b,
  input  a_2,
  input  b_2,
  output a___b,
  output a___b_2
);

  wire nand_1_out, nor_1_out, nor_2_out;

  nand nand_1 (nand_1_out, a, b);
  nor nor_1 (nor_1_out, a_2, a_2);
  nor nor_2 (nor_2_out, b_2, b_2);
  nand nand_2 (a___b, nand_1_out, nand_1_out);
  nor nor_3 (a___b_2, nor_1_out, nor_2_out);
endmodule

module OR (
  input  a,
  input  b,
  input  a_2,
  input  b_2,
  output a___b,
  output a___b_2
);

  wire nand_1_out, nand_2_out, nor_1_out;

  nor nor_1 (nor_1_out, a, b);
  nand nand_1 (nand_1_out, a_2, a_2);
  nand nand_2 (nand_2_out, b_2, b_2);
  nor nor_2 (a___b, nor_1_out, nor_1_out);
  nand nand_3 (a___b_2, nand_1_out, nand_2_out);
endmodule

module XOR___NOR (
  input  a,
  input  b,
  input  a_2,
  input  b_2,
  output a_xor_b,
  output a_xor_b_2
);

  wire nor_1_out, nor_2_out, nor_3_out, nor_4_out, nor_5_out, nor_6_out, nor_7_out, nor_8_out, nor_10_out;

  nor nor_1 (nor_1_out, b, b);
  nor nor_2 (nor_2_out, a, a);
  nor nor_3 (nor_3_out, b_2, b_2);
  nor nor_4 (nor_4_out, a_2, a_2);
  nor nor_5 (nor_5_out, nor_1_out, a);
  nor nor_6 (nor_6_out, b, nor_2_out);
  nor nor_7 (nor_7_out, nor_3_out, nor_4_out);
  nor nor_8 (nor_8_out, b_2, a_2);
  nor nor_9 (a_xor_b, nor_10_out, nor_10_out);
  nor nor_10 (nor_10_out, nor_5_out, nor_6_out);
  nor nor_11 (a_xor_b_2, nor_7_out, nor_8_out);

  // Notes on the sheet:
  //   Lembrando que$        a xor b$       e igual a$( a . b' ) + ( a' . b )
endmodule

module XOR___NAND (
  input  a,
  input  b,
  input  a_2,
  input  b_2,
  output a_xor_b,
  output a_xor_b_2
);

  wire nand_1_out, nand_2_out, nand_3_out, nand_4_out, nand_5_out, nand_6_out, nand_7_out;

  nand nand_1 (nand_1_out, b, b);
  nand nand_2 (nand_2_out, a, a);
  nand nand_3 (nand_3_out, b_2, a_2);
  nand nand_4 (nand_4_out, a, nand_1_out);
  nand nand_5 (nand_5_out, nand_2_out, b);
  nand nand_6 (nand_6_out, b_2, nand_3_out);
  nand nand_7 (nand_7_out, nand_3_out, a_2);
  nand nand_8 (a_xor_b, nand_4_out, nand_5_out);
  nand nand_9 (a_xor_b_2, nand_6_out, nand_7_out);
endmodule
