// Logisim project Somadores_Subtratores.circ as structural Verilog: 6 circuits, main circuit meio somador
module meio_somador (
  input  a,
  input  b,
  output s0,
  output vai1
);

  and and_1 (vai1, a, b);
  xor xor_1 (s0, a, b);

  // Notes on the sheet:
  //   Clicar em Project->Analyze Circuit para ver a tabela-verdade
endmodule

module somador_completo (
  input  vem1,
  input  a,
  input  b,
  output s0,
  output vai1
);

  wire meio_somador_1_s0, meio_somador_1_vai1, meio_somador_2_vai1;

  meio_somador meio_somador_1 (.a(a), .b(b), .s0(meio_somador_1_s0), .vai1(meio_somador_1_vai1));
  meio_somador meio_somador_2 (.a(meio_somador_1_s0), .b(vem1), .s0(s0), .vai1(meio_somador_2_vai1));
  or or_1 (vai1, meio_somador_2_vai1, meio_somador_1_vai1);

  // Notes on the sheet:
  //   +/2  = Meio Somador
endmodule

module somador_de_4 (
  input  [3:0] a,
  input  [3:0] b,
  input  vem1,
  output [3:0] s,
  output [4:0] s_2,
  output vai1
);

  wire somador_completo_1_vai1, somador_completo_2_vai1, somador_completo_3_vai1;

  // Probe on a
  // Probe on b
  somador_completo somador_completo_1 (.vem1(vem1), .a(b[0]), .b(a[0]), .s0(s[0]), .vai1(somador_completo_1_vai1));
  somador_completo somador_completo_2 (
    .vem1(somador_completo_1_vai1), .a(b[1]), .b(a[1]), .s0(s[1]), .vai1(somador_completo_2_vai1));
  somador_completo somador_completo_3 (
    .vem1(somador_completo_2_vai1), .a(b[2]), .b(a[2]), .s0(s[2]), .vai1(somador_completo_3_vai1));
  somador_completo somador_completo_4 (.vem1(somador_completo_3_vai1), .a(b[3]), .b(a[3]), .s0(s[3]), .vai1(s_2[4]));
  // Probe on s
  // Probe on {s_2[4], s}

  assign s_2[3:0] = s;
  assign vai1 = s_2[4];

  // Notes on the sheet:
  //   Ao somar números de N bits, o resultado terá N+1 bits
  //   O bit excedente poderá ser tratado como overflow
  //   Ou incluido no resultado
endmodule

module meio_subrator (
  input  a,
  input  b,
  output s,
  output deve1
);

  wire not_1_out;

  not not_1 (not_1_out, a);
  xor xor_1 (s, a, b);
  and and_1 (deve1, not_1_out, b);
endmodule

module subtrator_ccompleto (
  input  vem_um,
  input  a,
  input  b,
  output s0,
  output deve_um
);

  wire meio_subrator_1_deve1, meio_subrator_1_s, meio_subrator_2_deve1;

  meio_subrator meio_subrator_1 (.a(a), .b(b), .s(meio_subrator_1_s), .deve1(meio_subrator_1_deve1));
  meio_subrator meio_subrator_2 (.a(meio_subrator_1_s), .b(vem_um), .s(s0), .deve1(meio_subrator_2_deve1));
  or or_1 (deve_um, meio_subrator_2_deve1, meio_subrator_1_deve1);
endmodule

module Subtrator_de_4 (
  input  [3:0] a,
  input  [3:0] b,
  input  vem1,
  output [3:0] s,
  output deve_um
);

  wire subtrator_ccompleto_1_deve_um, subtrator_ccompleto_2_deve_um, subtrator_ccompleto_3_deve_um;

  // Probe on a
  // Probe on b
  subtrator_ccompleto subtrator_ccompleto_1 (
    .vem_um(vem1), .a(a[0]), .b(b[0]), .s0(s[0]), .deve_um(subtrator_ccompleto_1_deve_um));
  subtrator_ccompleto subtrator_ccompleto_2 (
    .vem_um(subtrator_ccompleto_1_deve_um), .a(a[1]), .b(b[1]), .s0(s[1]),
    .deve_um(subtrator_ccompleto_2_deve_um));
  subtrator_ccompleto subtrator_ccompleto_3 (
    .vem_um(subtrator_ccompleto_2_deve_um), .a(a[2]), .b(b[2]), .s0(s[2]),
    .deve_um(subtrator_ccompleto_3_deve_um));
  subtrator_ccompleto subtrator_ccompleto_4 (
    .vem_um(subtrator_ccompleto_3_deve_um), .a(a[3]), .b(b[3]), .s0(s[3]), .deve_um(deve_um));
  // Probe on s
endmodule
